// Logisim project alu.circ as structural Verilog: 5 circuits, main circuit main
module main (
  input  [2:0] opcode,
  input  [7:0] x,
  input  [7:0] y,
  output [7:0] result,
  output SF,
  output ZF,
  output CF,
  output OF,
  output EQ
);

  wire [7:0] alu_1_addition;

  ALU alu_1 (
    .X(x), .Y(y), .Opcode(opcode), .Addition(alu_1_addition), .And(alu_1_addition), .Or(alu_1_addition),
    .Subtraction(alu_1_addition), .Result(result), .out_10(alu_1_addition[0]), .L_Left(alu_1_addition),
    .L_Right(alu_1_addition), .A_Right(alu_1_addition), .X___Y(alu_1_addition), .EQ(EQ), .CF(CF), .OF(OF),
    .SF(SF), .ZF(ZF));  // open: out_8
  // Pins of 1 and 8 bits meet at alu_1_addition
endmodule

module Adder (
  input  [7:0] X,
  input  [7:0] Y,
  output [7:0] \output ,
  output Cout
);

  Adder_part adder_1 (.a(X), .b(Y), .out(\output ), .cin(1'b0), .cout(Cout));
endmodule

module Register_File (
  input  [7:0] X,
  input  [7:0] Y
);
endmodule

module Subtractor (
  input  [7:0] X,
  input  [7:0] Y,
  output [7:0] out_3,
  output out_4
);

  wire [7:0] not_1_out;

  Adder adder_1 (.X(X), .Y(not_1_out), .Cout(out_4), .\output (out_3));
  assign not_1_out = ~Y;  // NOT_Gate not_1, 8 bits wide
endmodule

module ALU (
  input  [7:0] X,
  input  [7:0] Y,
  input  [2:0] Opcode,
  output [7:0] Addition,
  output [7:0] And,
  output [7:0] Or,
  output [7:0] Subtraction,
  output out_8,
  output [7:0] Result,
  output out_10,
  output [7:0] L_Left,
  output [7:0] L_Right,
  output [7:0] A_Right,
  output [7:0] X___Y,
  output EQ,
  output ZF,
  output SF,
  output OF,
  output CF
);

  wire and_2_out, comparator_1_gt, comparator_3_eq, comparator_4_eq, nand_1_out, nand_2_out, nor_out,
       not_1_out, not_2_out, not_3_out, or_1_out, or_3_out;

  not not_1 (not_1_out, out_10);
  and and_1 (CF, out_8, not_1_out);
  and and_2 (and_2_out, Y[7], X[7]);
  nand nand_1 (nand_1_out, and_2_out, Result[7]);
  or or_1 (or_1_out, nand_1_out, nand_2_out);
  nor \nor  (nor_out, Y[7], X[7]);
  nand nand_2 (nand_2_out, nor_out, Result[7]);
  and and_3 (OF, or_1_out, or_3_out);
  assign Or = X | Y;  // OR_Gate or_2, 8 bits wide
  assign And = X & Y;  // AND_Gate and_4, 8 bits wide
  Adder adder_1 (.X(X), .Y(Y), .Cout(out_8), .\output (Addition));
  Subtractor subtractor_1 (.X(X), .Y(Y), .out_3(Subtraction), .out_4(out_10));
  not not_2 (not_2_out, Y[7]);
  // AND_Gate and_5 has open pins: in0=not_2_out, in1=X[7], out=open
  Shifter shifter_1 (.in(X), .\dist (Y[2:0]), .out(L_Left));
  Shifter #(.shift("lr")) shifter_2 (.in(X), .\dist (Y[2:0]), .out(L_Right));
  Shifter #(.shift("ar")) shifter_3 (.in(X), .\dist (Y[2:0]), .out(A_Right));
  Comparator comparator_1 (.a(X), .b(Y), .gt(comparator_1_gt));  // open: eq, lt
  Comparator comparator_2 (.a(Y), .b(X), .eq(EQ));  // open: gt, lt
  not not_3 (not_3_out, X[7]);
  // NAND_Gate nand_3 has open pins: in0=Y[7], in1=not_3_out, out=open
  not not_4 (SF, Result[7]);
  assign X___Y = {{7{1'b0}}, comparator_1_gt};  // Bit_Extender bit_extender_1
  nor nor_2 (ZF, Result[7], Result[6], Result[5], Result[4], Result[3], Result[2], Result[1], Result[0]);
  Multiplexer #(.select(3), .width(8), .enable("false")) multiplexer_1 (
    .in0(Or), .in1(And), .in2(Addition), .in3(Subtraction), .in4(L_Left), .in5(L_Right), .in6(A_Right),
    .in7(X___Y), .out(Result), .sel(Opcode));
  Comparator #(.width(3)) comparator_3 (.a(3'b010), .b(Opcode), .eq(comparator_3_eq));  // open: gt, lt
  Comparator #(.width(3)) comparator_4 (.a(3'b011), .b(Opcode), .eq(comparator_4_eq));  // open: gt, lt
  or or_3 (or_3_out, comparator_3_eq, comparator_4_eq);

  // Notes on the sheet:
  //   cs31 lab3, part 2: ALU
endmodule
