// Logisim project part1.circ as structural Verilog: 4 circuits, main circuit main
module main (
  input  [3:0] X,
  input  [1:0] Y,
  input  C_in,
  output [3:0] Sum,
  output C_out
);

  wire [3:0] signext2to4_output1;

  signex2to4 signext2to4 (.input1(Y), .output1(signext2to4_output1));
  fulladder4 fulladder4 (.C_in(C_in), .X(X), .Y(signext2to4_output1), .Sum(Sum), .Cout(C_out));

  // Notes on the sheet:
  //   cs31 lab3, part 1
endmodule

module signex2to4 (
  input  [1:0] input1,
  output [3:0] output1
);


  assign output1 = {{3{input1[1]}}, input1[0]};
endmodule

module fulladder (
  input  A,
  input  B,
  input  C,
  output S,
  output Cout
);

  wire and_1_out, and_2_out, xor_1_out;

  xor xor_1 (xor_1_out, A, B);
  and and_1 (and_1_out, A, B);
  xor xor_2 (S, xor_1_out, C);
  and and_2 (and_2_out, xor_1_out, C);
  or or_1 (Cout, and_2_out, and_1_out);
endmodule

module fulladder4 (
  input  C_in,
  input  [3:0] X,
  input  [3:0] Y,
  output [3:0] Sum,
  output Cout
);

  wire fulladder_1_cout, fulladder_2_cout, fulladder_3_cout;

  fulladder fulladder_1 (.A(X[0]), .B(Y[0]), .C(C_in), .S(Sum[0]), .Cout(fulladder_1_cout));
  fulladder fulladder_2 (.A(X[1]), .B(Y[1]), .C(fulladder_1_cout), .S(Sum[1]), .Cout(fulladder_2_cout));
  fulladder fulladder_3 (.A(X[2]), .B(Y[2]), .C(fulladder_2_cout), .S(Sum[2]), .Cout(fulladder_3_cout));
  fulladder fulladder_4 (.A(X[3]), .B(Y[3]), .C(fulladder_3_cout), .S(Sum[3]), .Cout(Cout));
endmodule
